// Logisim project DMX.circ as structural Verilog: 1 circuit, main circuit main
module main (
);

  wire [4:0] joystick_1_x, joystick_1_y;
  wire [30:0] decoder_1_out31, demultiplexer_1_out1, demultiplexer_1_out2, demultiplexer_1_out3,
       demultiplexer_1_out4, demultiplexer_1_out5, demultiplexer_1_out6, demultiplexer_1_out7,
       demultiplexer_1_out8, demultiplexer_1_out9, demultiplexer_1_out10, demultiplexer_1_out11,
       demultiplexer_1_out12, demultiplexer_1_out13, demultiplexer_1_out14, demultiplexer_1_out15,
       demultiplexer_1_out16, demultiplexer_1_out17, demultiplexer_1_out18, demultiplexer_1_out19,
       demultiplexer_1_out20, demultiplexer_1_out21, demultiplexer_1_out22, demultiplexer_1_out23,
       demultiplexer_1_out24, demultiplexer_1_out25, demultiplexer_1_out26, demultiplexer_1_out27,
       demultiplexer_1_out28, demultiplexer_1_out29, demultiplexer_1_out30, demultiplexer_1_out31;

  DotMatrix #(.matrixcols(31), .matrixrows(31)) dotmatrix_1 (
    .col0(demultiplexer_1_out1), .col1(demultiplexer_1_out2), .col2(demultiplexer_1_out3),
    .col3(demultiplexer_1_out4), .col4(demultiplexer_1_out5), .col5(demultiplexer_1_out6),
    .col6(demultiplexer_1_out7), .col7(demultiplexer_1_out8), .col8(demultiplexer_1_out9),
    .col9(demultiplexer_1_out10), .col10(demultiplexer_1_out11), .col11(demultiplexer_1_out12),
    .col12(demultiplexer_1_out13), .col13(demultiplexer_1_out14), .col14(demultiplexer_1_out15),
    .col15(demultiplexer_1_out16), .col16(demultiplexer_1_out17), .col17(demultiplexer_1_out18),
    .col18(demultiplexer_1_out19), .col19(demultiplexer_1_out20), .col20(demultiplexer_1_out21),
    .col21(demultiplexer_1_out22), .col22(demultiplexer_1_out23), .col23(demultiplexer_1_out24),
    .col24(demultiplexer_1_out25), .col25(demultiplexer_1_out26), .col26(demultiplexer_1_out27),
    .col27(demultiplexer_1_out28), .col28(demultiplexer_1_out29), .col29(demultiplexer_1_out30),
    .col30(demultiplexer_1_out31));
  Joystick #(.bits(5)) joystick_1 (.x(joystick_1_x), .y(joystick_1_y));
  Decoder #(.select(5)) decoder_1 (
    .out1(decoder_1_out31[30]), .out2(decoder_1_out31[29]), .out3(decoder_1_out31[28]),
    .out4(decoder_1_out31[27]), .out5(decoder_1_out31[26]), .out6(decoder_1_out31[25]),
    .out7(decoder_1_out31[24]), .out8(decoder_1_out31[23]), .out9(decoder_1_out31[22]),
    .out10(decoder_1_out31[21]), .out11(decoder_1_out31[20]), .out12(decoder_1_out31[19]),
    .out13(decoder_1_out31[18]), .out14(decoder_1_out31[17]), .out15(decoder_1_out31[16]),
    .out16(decoder_1_out31[15]), .out17(decoder_1_out31[14]), .out18(decoder_1_out31[13]),
    .out19(decoder_1_out31[12]), .out20(decoder_1_out31[11]), .out21(decoder_1_out31[10]),
    .out22(decoder_1_out31[9]), .out23(decoder_1_out31[8]), .out24(decoder_1_out31[7]),
    .out25(decoder_1_out31[6]), .out26(decoder_1_out31[5]), .out27(decoder_1_out31[4]),
    .out28(decoder_1_out31[3]), .out29(decoder_1_out31[2]), .out30(decoder_1_out31[1]),
    .out31(decoder_1_out31[0]), .sel(joystick_1_y));  // open: out0, en
  Demultiplexer #(.select(5), .width(31)) demultiplexer_1 (
    .out1(demultiplexer_1_out1), .out2(demultiplexer_1_out2), .out3(demultiplexer_1_out3),
    .out4(demultiplexer_1_out4), .out5(demultiplexer_1_out5), .out6(demultiplexer_1_out6),
    .out7(demultiplexer_1_out7), .out8(demultiplexer_1_out8), .out9(demultiplexer_1_out9),
    .out10(demultiplexer_1_out10), .out11(demultiplexer_1_out11), .out12(demultiplexer_1_out12),
    .out13(demultiplexer_1_out13), .out14(demultiplexer_1_out14), .out15(demultiplexer_1_out15),
    .out16(demultiplexer_1_out16), .out17(demultiplexer_1_out17), .out18(demultiplexer_1_out18),
    .out19(demultiplexer_1_out19), .out20(demultiplexer_1_out20), .out21(demultiplexer_1_out21),
    .out22(demultiplexer_1_out22), .out23(demultiplexer_1_out23), .out24(demultiplexer_1_out24),
    .out25(demultiplexer_1_out25), .out26(demultiplexer_1_out26), .out27(demultiplexer_1_out27),
    .out28(demultiplexer_1_out28), .out29(demultiplexer_1_out29), .out30(demultiplexer_1_out30),
    .out31(demultiplexer_1_out31), .in(decoder_1_out31), .sel(joystick_1_x));  // open: out0, en
endmodule
