// Logisim project Tetris.circ as structural Verilog: 4 circuits, main circuit main
module main (
);

  DotMatrix #(.matrixcols(10), .matrixrows(20)) dotmatrix_1 ();  // open: col0, col1, col2, col3, col4, col5, col6, col7, col8, col9
  Button R ();  // open: out
  Button button ();  // open: out
  Button button_2 ();  // open: out
  Button V ();  // open: out
  DotMatrix #(.matrixrows(5)) dotmatrix_2 ();  // open: col0, col1, col2, col3, col4
endmodule

module drivr (
  input  Rotate,
  input  Left,
  input  Right,
  input  Drop,
  input  Start,
  input  Pause,
  output [19:0] out_7,
  output [19:0] out_8,
  output [19:0] out_9,
  output [19:0] out_10,
  output [19:0] out_11,
  output [19:0] out_12,
  output [19:0] out_13,
  output [19:0] out_14,
  output [19:0] out_15,
  output [19:0] out_16
);

  wire Clock, clock_1_out, not_1_out, or_2_out, Present, Score, Spawn, step_1_lodge, t_ff_1_qn;
  wire [3:0] counter_1_q;
  wire [19:0] controlled_buffer_1_out, controlled_buffer_2_out, controlled_buffer_3_out,
       controlled_buffer_4_out, controlled_buffer_5_out, controlled_buffer_6_out, controlled_buffer_7_out,
       controlled_buffer_8_out, controlled_buffer_9_out, controlled_buffer_10_out, register_1_q,
       register_2_q, register_3_q, register_4_q, register_5_q, register_6_q, register_7_q, register_8_q,
       register_9_q, register_10_q, register_11_q, register_12_q, register_13_q, register_14_q,
       register_15_q, register_16_q, register_17_q, register_18_q, register_19_q, register_20_q,
       spawn_1_out_2, spawn_1_out_3, spawn_1_out_4, spawn_1_out_5, spawn_1_out_6, spawn_1_out_7,
       spawn_1_out_8, spawn_1_out_9, spawn_1_out_10, spawn_1_out_11, step_1_out_21, step_1_out_22,
       step_1_out_23, step_1_out_24, step_1_out_25, step_1_out_26, step_1_out_27, step_1_out_28,
       step_1_out_29, step_1_out_30, step_1_out_31, step_1_out_32, step_1_out_33, step_1_out_34,
       step_1_out_35, step_1_out_36, step_1_out_37, step_1_out_38, step_1_out_39, step_1_out_40;

  not not_1 (not_1_out, Spawn);
  assign controlled_buffer_1_out = Spawn ? spawn_1_out_2 : 20'bz;  // Controlled_Buffer controlled_buffer_1
  Spawn spawn_1 (
    .Start(Spawn), .out_2(spawn_1_out_2), .out_3(spawn_1_out_3), .out_4(spawn_1_out_4),
    .out_5(spawn_1_out_5), .out_6(spawn_1_out_6), .out_7(spawn_1_out_7), .out_8(spawn_1_out_8),
    .out_9(spawn_1_out_9), .out_10(spawn_1_out_10), .out_11(spawn_1_out_11));  // open: Spawn_Data_1, Spawn_Data_2
  assign controlled_buffer_2_out = Spawn ? spawn_1_out_3 : 20'bz;  // Controlled_Buffer controlled_buffer_2
  assign controlled_buffer_3_out = Spawn ? spawn_1_out_4 : 20'bz;  // Controlled_Buffer controlled_buffer_3
  assign controlled_buffer_4_out = Spawn ? spawn_1_out_5 : 20'bz;  // Controlled_Buffer controlled_buffer_4
  assign controlled_buffer_5_out = Spawn ? spawn_1_out_6 : 20'bz;  // Controlled_Buffer controlled_buffer_5
  assign controlled_buffer_6_out = Spawn ? spawn_1_out_7 : 20'bz;  // Controlled_Buffer controlled_buffer_6
  assign controlled_buffer_7_out = Spawn ? spawn_1_out_8 : 20'bz;  // Controlled_Buffer controlled_buffer_7
  assign controlled_buffer_8_out = Spawn ? spawn_1_out_9 : 20'bz;  // Controlled_Buffer controlled_buffer_8
  assign controlled_buffer_9_out = Spawn ? spawn_1_out_10 : 20'bz;  // Controlled_Buffer controlled_buffer_9
  assign controlled_buffer_10_out = Spawn ? spawn_1_out_11 : 20'bz;  // Controlled_Buffer controlled_buffer_10
  assign controlled_buffer_10_out = not_1_out ? step_1_out_40 : 20'bz;  // Controlled_Buffer controlled_buffer_11
  assign controlled_buffer_4_out = not_1_out ? step_1_out_34 : 20'bz;  // Controlled_Buffer controlled_buffer_12
  assign controlled_buffer_3_out = not_1_out ? step_1_out_33 : 20'bz;  // Controlled_Buffer controlled_buffer_13
  assign controlled_buffer_7_out = not_1_out ? step_1_out_37 : 20'bz;  // Controlled_Buffer controlled_buffer_14
  assign controlled_buffer_2_out = not_1_out ? step_1_out_32 : 20'bz;  // Controlled_Buffer controlled_buffer_15
  assign controlled_buffer_5_out = not_1_out ? step_1_out_35 : 20'bz;  // Controlled_Buffer controlled_buffer_16
  assign controlled_buffer_8_out = not_1_out ? step_1_out_38 : 20'bz;  // Controlled_Buffer controlled_buffer_17
  assign controlled_buffer_6_out = not_1_out ? step_1_out_36 : 20'bz;  // Controlled_Buffer controlled_buffer_18
  assign controlled_buffer_9_out = not_1_out ? step_1_out_39 : 20'bz;  // Controlled_Buffer controlled_buffer_19
  assign controlled_buffer_1_out = not_1_out ? step_1_out_31 : 20'bz;  // Controlled_Buffer controlled_buffer_20
  Step step_1 (
    .Lodge(step_1_lodge), .in_1(register_1_q), .in_2(register_2_q), .in_3(register_3_q), .in_4(register_4_q),
    .in_5(register_5_q), .in_6(register_6_q), .in_7(register_7_q), .in_8(register_8_q), .in_9(register_9_q),
    .in_10(register_10_q), .in_11(register_11_q), .in_12(register_12_q), .in_13(register_13_q),
    .in_14(register_14_q), .in_15(register_15_q), .in_16(register_16_q), .in_17(register_17_q),
    .in_18(register_18_q), .in_19(register_19_q), .in_20(register_20_q), .out_21(step_1_out_21),
    .out_22(step_1_out_22), .out_23(step_1_out_23), .out_24(step_1_out_24), .out_25(step_1_out_25),
    .out_26(step_1_out_26), .out_27(step_1_out_27), .out_28(step_1_out_28), .out_29(step_1_out_29),
    .out_30(step_1_out_30), .out_31(step_1_out_31), .out_32(step_1_out_32), .out_33(step_1_out_33),
    .out_34(step_1_out_34), .out_35(step_1_out_35), .out_36(step_1_out_36), .out_37(step_1_out_37),
    .out_38(step_1_out_38), .out_39(step_1_out_39), .out_40(step_1_out_40));
  or or_1 (Spawn, Start, step_1_lodge);
  Register #(.width(20)) register_1 (
    .D(controlled_buffer_1_out), .Q(register_1_q), .clk(or_2_out), .clr(Start));  // open: en
  Register #(.width(20)) register_2 (
    .D(controlled_buffer_2_out), .Q(register_2_q), .clk(or_2_out), .clr(Start));  // open: en
  Register #(.width(20)) register_3 (
    .D(controlled_buffer_3_out), .Q(register_3_q), .clk(or_2_out), .clr(Start));  // open: en
  Register #(.width(20)) register_4 (
    .D(controlled_buffer_4_out), .Q(register_4_q), .clk(or_2_out), .clr(Start));  // open: en
  Register #(.width(20)) register_5 (
    .D(controlled_buffer_5_out), .Q(register_5_q), .clk(or_2_out), .clr(Start));  // open: en
  Register #(.width(20)) register_6 (
    .D(controlled_buffer_6_out), .Q(register_6_q), .clk(or_2_out), .clr(Start));  // open: en
  Register #(.width(20)) register_7 (
    .D(controlled_buffer_7_out), .Q(register_7_q), .clk(or_2_out), .clr(Start));  // open: en
  Register #(.width(20)) register_8 (
    .D(controlled_buffer_8_out), .Q(register_8_q), .clk(or_2_out), .clr(Start));  // open: en
  Register #(.width(20)) register_9 (
    .D(controlled_buffer_9_out), .Q(register_9_q), .clk(or_2_out), .clr(Start));  // open: en
  Register #(.width(20)) register_10 (
    .D(controlled_buffer_10_out), .Q(register_10_q), .clk(or_2_out), .clr(Start));  // open: en
  or or_2 (or_2_out, Clock, Score);
  Register #(.width(20)) register_11 (.D(step_1_out_30), .Q(register_11_q), .clk(or_2_out), .clr(Start));  // open: en
  Register #(.width(20)) register_12 (.D(step_1_out_29), .Q(register_12_q), .clk(or_2_out), .clr(Start));  // open: en
  Register #(.width(20)) register_13 (.D(step_1_out_28), .Q(register_13_q), .clk(or_2_out), .clr(Start));  // open: en
  Register #(.width(20)) register_14 (.D(step_1_out_27), .Q(register_14_q), .clk(or_2_out), .clr(Start));  // open: en
  Register #(.width(20)) register_15 (.D(step_1_out_26), .Q(register_15_q), .clk(or_2_out), .clr(Start));  // open: en
  Register #(.width(20)) register_16 (.D(step_1_out_25), .Q(register_16_q), .clk(or_2_out), .clr(Start));  // open: en
  Register #(.width(20)) register_17 (.D(step_1_out_24), .Q(register_17_q), .clk(or_2_out), .clr(Start));  // open: en
  Register #(.width(20)) register_18 (.D(step_1_out_23), .Q(register_18_q), .clk(or_2_out), .clr(Start));  // open: en
  Register #(.width(20)) register_19 (.D(step_1_out_22), .Q(register_19_q), .clk(or_2_out), .clr(Start));  // open: en
  Register #(.width(20)) register_20 (.D(step_1_out_21), .Q(register_20_q), .clk(or_2_out), .clr(Start));  // open: en
  and and_1 (Score, register_20_q[19], register_19_q[19], register_18_q[19], register_17_q[19], register_16_q[19], register_15_q[19], register_14_q[19], register_13_q[19], register_12_q[19], register_11_q[19]);
  Register #(.width(20), .trigger("falling")) register_21 (.clk(Clock));  // open: D, en, Q, clr
  Register #(.width(20), .trigger("falling")) register_22 (.clk(Clock));  // open: D, en, Q, clr
  Register #(.width(20), .trigger("falling")) register_23 (.clk(Clock));  // open: D, en, Q, clr
  Register #(.width(20), .trigger("falling")) register_24 (.clk(Clock));  // open: D, en, Q, clr
  Register #(.width(20), .trigger("falling")) register_25 (.clk(Clock));  // open: D, en, Q, clr
  Register #(.width(20), .trigger("falling")) register_26 (.clk(Clock));  // open: D, en, Q, clr
  Register #(.width(20), .trigger("falling")) register_27 (.clk(Clock));  // open: D, en, Q, clr
  Register #(.width(20), .trigger("falling")) register_28 (.clk(Clock));  // open: D, en, Q, clr
  Register #(.width(20), .trigger("falling")) register_29 (.clk(Clock));  // open: D, en, Q, clr
  Register #(.width(20), .trigger("falling")) register_30 (.clk(Clock));  // open: D, en, Q, clr
  Counter #(.width(4), .max('hf), .ongoal("continue")) counter_1 (
    .count(Score), .Q(counter_1_q), .clk(Score));  // open: load, D, carry, clr
  Hex_Digit_Display hex_digit_display_1 (.value(counter_1_q), .dp(Start));
  T_Flip_Flop t_ff_1 (.clk(Pause), .T(Pause), .Qn(t_ff_1_qn));  // open: Q, preset, reset, en
  Button button_1 ();  // open: out
  Clock clock_1 (.out(clock_1_out));
  and and_2 (Clock, t_ff_1_qn, clock_1_out);
  not not_2 (Present, Start);

  // Notes on the sheet:
  //   obj
  //   BG
endmodule

module Spawn (
  input  Start,
  output [19:0] out_2,
  output [19:0] out_3,
  output [19:0] out_4,
  output [19:0] out_5,
  output [19:0] out_6,
  output [19:0] out_7,
  output [19:0] out_8,
  output [19:0] out_9,
  output [19:0] out_10,
  output [19:0] out_11,
  output [9:0] Spawn_Data_1,
  output [9:0] Spawn_Data_2
);

  wire button_1_out, decoder_1_out0, decoder_1_out1, decoder_1_out2, decoder_1_out3, decoder_1_out4,
       decoder_1_out5, decoder_1_out6, decoder_1_out7, or_1_out;
  wire [2:0] Piece_chooser_out;

  Button button_1 (.out(button_1_out));
  Random #(.width(3)) Piece_chooser (.clk(button_1_out), .out(Piece_chooser_out));  // open: next, clr
  Decoder #(.select(3)) decoder_1 (
    .out0(decoder_1_out0), .out1(decoder_1_out1), .out2(decoder_1_out2), .out3(decoder_1_out3),
    .out4(decoder_1_out4), .out5(decoder_1_out5), .out6(decoder_1_out6), .out7(decoder_1_out7),
    .sel(Piece_chooser_out));  // open: en
  or or_1 (or_1_out, decoder_1_out6, decoder_1_out7);
  assign {out_11[19], out_10[19], out_9[19], out_8[19], out_7[19], out_6[19], out_5[19], out_4[19], out_3[19], out_2[19]} = decoder_1_out0 ? 10'h30 : 10'bz;  // Controlled_Buffer controlled_buffer_1
  assign {out_11[18], out_10[18], out_9[18], out_8[18], out_7[18], out_6[18], out_5[18], out_4[18], out_3[18], out_2[18]} = decoder_1_out0 ? 10'h30 : 10'bz;  // Controlled_Buffer controlled_buffer_2
  assign {out_11[19], out_10[19], out_9[19], out_8[19], out_7[19], out_6[19], out_5[19], out_4[19], out_3[19], out_2[19]} = decoder_1_out1 ? 10'h70 : 10'bz;  // Controlled_Buffer controlled_buffer_3
  assign {out_11[18], out_10[18], out_9[18], out_8[18], out_7[18], out_6[18], out_5[18], out_4[18], out_3[18], out_2[18]} = decoder_1_out1 ? 10'h38 : 10'bz;  // Controlled_Buffer controlled_buffer_4
  assign {out_11[19], out_10[19], out_9[19], out_8[19], out_7[19], out_6[19], out_5[19], out_4[19], out_3[19], out_2[19]} = decoder_1_out2 ? 10'h38 : 10'bz;  // Controlled_Buffer controlled_buffer_5
  assign {out_11[18], out_10[18], out_9[18], out_8[18], out_7[18], out_6[18], out_5[18], out_4[18], out_3[18], out_2[18]} = decoder_1_out2 ? 10'h70 : 10'bz;  // Controlled_Buffer controlled_buffer_6
  assign {out_11[19], out_10[19], out_9[19], out_8[19], out_7[19], out_6[19], out_5[19], out_4[19], out_3[19], out_2[19]} = decoder_1_out3 ? {10{1'b0}} : 10'bz;  // Controlled_Buffer controlled_buffer_7
  assign {out_11[18], out_10[18], out_9[18], out_8[18], out_7[18], out_6[18], out_5[18], out_4[18], out_3[18], out_2[18]} = decoder_1_out3 ? 10'h78 : 10'bz;  // Controlled_Buffer controlled_buffer_8
  assign {out_11[19], out_10[19], out_9[19], out_8[19], out_7[19], out_6[19], out_5[19], out_4[19], out_3[19], out_2[19]} = decoder_1_out4 ? 10'h20 : 10'bz;  // Controlled_Buffer controlled_buffer_9
  assign {out_11[18], out_10[18], out_9[18], out_8[18], out_7[18], out_6[18], out_5[18], out_4[18], out_3[18], out_2[18]} = decoder_1_out4 ? 10'h38 : 10'bz;  // Controlled_Buffer controlled_buffer_10
  assign {out_11[19], out_10[19], out_9[19], out_8[19], out_7[19], out_6[19], out_5[19], out_4[19], out_3[19], out_2[19]} = decoder_1_out5 ? 10'h10 : 10'bz;  // Controlled_Buffer controlled_buffer_11
  assign {out_11[18], out_10[18], out_9[18], out_8[18], out_7[18], out_6[18], out_5[18], out_4[18], out_3[18], out_2[18]} = decoder_1_out5 ? 10'h70 : 10'bz;  // Controlled_Buffer controlled_buffer_12
  assign {out_11[19], out_10[19], out_9[19], out_8[19], out_7[19], out_6[19], out_5[19], out_4[19], out_3[19], out_2[19]} = or_1_out ? 10'h20 : 10'bz;  // Controlled_Buffer controlled_buffer_13
  assign {out_11[18], out_10[18], out_9[18], out_8[18], out_7[18], out_6[18], out_5[18], out_4[18], out_3[18], out_2[18]} = or_1_out ? 10'h70 : 10'bz;  // Controlled_Buffer controlled_buffer_14

  assign out_2[17:0] = {18{1'b0}};
  assign out_3[17:0] = {18{1'b0}};
  assign out_4[17:0] = {18{1'b0}};
  assign out_5[17:0] = {18{1'b0}};
  assign out_6[17:0] = {18{1'b0}};
  assign out_7[17:0] = {18{1'b0}};
  assign out_8[17:0] = {18{1'b0}};
  assign out_9[17:0] = {18{1'b0}};
  assign out_10[17:0] = {18{1'b0}};
  assign out_11[17:0] = {18{1'b0}};
  assign Spawn_Data_1 = {out_11[19], out_10[19], out_9[19], out_8[19], out_7[19], out_6[19], out_5[19], out_4[19], out_3[19], out_2[19]};
  assign Spawn_Data_2 = {out_11[18], out_10[18], out_9[18], out_8[18], out_7[18], out_6[18], out_5[18], out_4[18], out_3[18], out_2[18]};
endmodule

module Step (
  input  [19:0] in_1,
  input  [19:0] in_2,
  input  [19:0] in_3,
  input  [19:0] in_4,
  input  [19:0] in_5,
  input  [19:0] in_6,
  input  [19:0] in_7,
  input  [19:0] in_8,
  input  [19:0] in_9,
  input  [19:0] in_10,
  input  [19:0] in_11,
  input  [19:0] in_12,
  input  [19:0] in_13,
  input  [19:0] in_14,
  input  [19:0] in_15,
  input  [19:0] in_16,
  input  [19:0] in_17,
  input  [19:0] in_18,
  input  [19:0] in_19,
  input  [19:0] in_20,
  output [19:0] out_21,
  output [19:0] out_22,
  output [19:0] out_23,
  output [19:0] out_24,
  output [19:0] out_25,
  output [19:0] out_26,
  output [19:0] out_27,
  output [19:0] out_28,
  output [19:0] out_29,
  output [19:0] out_30,
  output [19:0] out_31,
  output [19:0] out_32,
  output [19:0] out_33,
  output [19:0] out_34,
  output [19:0] out_35,
  output [19:0] out_36,
  output [19:0] out_37,
  output [19:0] out_38,
  output [19:0] out_39,
  output [19:0] out_40,
  output Lodge
);

  wire undriven;
  wire [19:0] adder_11_out, adder_12_out, adder_13_out, adder_14_out, adder_15_out, adder_16_out,
       adder_17_out, adder_18_out, adder_19_out, adder_20_out, shifter_1_out, shifter_2_out, shifter_3_out,
       shifter_4_out, shifter_5_out, shifter_6_out, shifter_7_out, shifter_8_out, shifter_9_out,
       shifter_10_out;

  Shifter #(.width(20), .shift("lr")) shifter_1 (.in(in_10), .\dist (5'b00001), .out(shifter_1_out));
  Shifter #(.width(20), .shift("lr")) shifter_2 (.in(in_9), .\dist (5'b00001), .out(shifter_2_out));
  Shifter #(.width(20), .shift("lr")) shifter_3 (.in(in_8), .\dist (5'b00001), .out(shifter_3_out));
  Shifter #(.width(20), .shift("lr")) shifter_4 (.in(in_7), .\dist (5'b00001), .out(shifter_4_out));
  Shifter #(.width(20), .shift("lr")) shifter_5 (.in(in_6), .\dist (5'b00001), .out(shifter_5_out));
  Shifter #(.width(20), .shift("lr")) shifter_6 (.in(in_5), .\dist (5'b00001), .out(shifter_6_out));
  Shifter #(.width(20), .shift("lr")) shifter_7 (.in(in_4), .\dist (5'b00001), .out(shifter_7_out));
  Shifter #(.width(20), .shift("lr")) shifter_8 (.in(in_3), .\dist (5'b00001), .out(shifter_8_out));
  Shifter #(.width(20), .shift("lr")) shifter_9 (.in(in_2), .\dist (5'b00001), .out(shifter_9_out));
  Shifter #(.width(20), .shift("lr")) shifter_10 (.in(in_1), .\dist (5'b00001), .out(shifter_10_out));
  Adder #(.width(20)) adder_1 (.a(in_20), .b(shifter_1_out));  // open: out, cin, cout
  Adder #(.width(20)) adder_2 (.a(in_19), .b(shifter_2_out));  // open: out, cin, cout
  Adder #(.width(20)) adder_3 (.a(in_18), .b(shifter_3_out));  // open: out, cin, cout
  Adder #(.width(20)) adder_4 (.a(in_17), .b(shifter_4_out));  // open: out, cin, cout
  Adder #(.width(20)) adder_5 (.a(in_16), .b(shifter_5_out));  // open: out, cin, cout
  Adder #(.width(20)) adder_6 (.a(in_15), .b(shifter_6_out));  // open: out, cin, cout
  Adder #(.width(20)) adder_7 (.a(in_14), .b(shifter_7_out));  // open: out, cin, cout
  Adder #(.width(20)) adder_8 (.a(in_13), .b(shifter_8_out));  // open: out, cin, cout
  Adder #(.width(20)) adder_9 (.a(in_12), .b(shifter_9_out));  // open: out, cin, cout
  Adder #(.width(20)) adder_10 (.a(in_11), .b(shifter_10_out));  // open: out, cin, cout
  Adder #(.width(20)) adder_11 (.a(in_20), .b(in_10), .out(adder_11_out));  // open: cin, cout
  Adder #(.width(20)) adder_12 (.a(in_19), .b(in_9), .out(adder_12_out));  // open: cin, cout
  Adder #(.width(20)) adder_13 (.a(in_18), .b(in_8), .out(adder_13_out));  // open: cin, cout
  Adder #(.width(20)) adder_14 (.a(in_17), .b(in_7), .out(adder_14_out));  // open: cin, cout
  Adder #(.width(20)) adder_15 (.a(in_16), .b(in_6), .out(adder_15_out));  // open: cin, cout
  Adder #(.width(20)) adder_16 (.a(in_15), .b(in_5), .out(adder_16_out));  // open: cin, cout
  Adder #(.width(20)) adder_17 (.a(in_14), .b(in_4), .out(adder_17_out));  // open: cin, cout
  Adder #(.width(20)) adder_18 (.a(in_13), .b(in_3), .out(adder_18_out));  // open: cin, cout
  Adder #(.width(20)) adder_19 (.a(in_12), .b(in_2), .out(adder_19_out));  // open: cin, cout
  Adder #(.width(20)) adder_20 (.a(in_11), .b(in_1), .out(adder_20_out));  // open: cin, cout
  Comparator comparator_1 ();  // open: a, b, gt, eq, lt
  assign out_31 = undriven ? shifter_1_out : 20'bz;  // Controlled_Buffer controlled_buffer_1
  assign out_32 = undriven ? shifter_2_out : 20'bz;  // Controlled_Buffer controlled_buffer_2
  assign out_33 = undriven ? shifter_3_out : 20'bz;  // Controlled_Buffer controlled_buffer_3
  assign out_34 = undriven ? shifter_4_out : 20'bz;  // Controlled_Buffer controlled_buffer_4
  assign out_35 = undriven ? shifter_5_out : 20'bz;  // Controlled_Buffer controlled_buffer_5
  assign out_36 = undriven ? shifter_6_out : 20'bz;  // Controlled_Buffer controlled_buffer_6
  assign out_37 = undriven ? shifter_7_out : 20'bz;  // Controlled_Buffer controlled_buffer_7
  assign out_38 = undriven ? shifter_8_out : 20'bz;  // Controlled_Buffer controlled_buffer_8
  assign out_39 = undriven ? shifter_9_out : 20'bz;  // Controlled_Buffer controlled_buffer_9
  assign out_40 = undriven ? shifter_10_out : 20'bz;  // Controlled_Buffer controlled_buffer_10
  assign out_21 = undriven ? in_20 : 20'bz;  // Controlled_Buffer controlled_buffer_11
  assign out_31 = Lodge ? {20{1'b0}} : 20'bz;  // Controlled_Buffer controlled_buffer_12
  assign out_22 = undriven ? in_19 : 20'bz;  // Controlled_Buffer controlled_buffer_13
  assign out_32 = Lodge ? {20{1'b0}} : 20'bz;  // Controlled_Buffer controlled_buffer_14
  assign out_23 = undriven ? in_18 : 20'bz;  // Controlled_Buffer controlled_buffer_15
  assign out_33 = Lodge ? {20{1'b0}} : 20'bz;  // Controlled_Buffer controlled_buffer_16
  assign out_24 = undriven ? in_17 : 20'bz;  // Controlled_Buffer controlled_buffer_17
  assign out_34 = Lodge ? {20{1'b0}} : 20'bz;  // Controlled_Buffer controlled_buffer_18
  assign out_25 = undriven ? in_16 : 20'bz;  // Controlled_Buffer controlled_buffer_19
  assign out_35 = Lodge ? {20{1'b0}} : 20'bz;  // Controlled_Buffer controlled_buffer_20
  assign out_26 = undriven ? in_15 : 20'bz;  // Controlled_Buffer controlled_buffer_21
  assign out_36 = Lodge ? {20{1'b0}} : 20'bz;  // Controlled_Buffer controlled_buffer_22
  assign out_27 = undriven ? in_14 : 20'bz;  // Controlled_Buffer controlled_buffer_23
  assign out_37 = Lodge ? {20{1'b0}} : 20'bz;  // Controlled_Buffer controlled_buffer_24
  assign out_28 = undriven ? in_13 : 20'bz;  // Controlled_Buffer controlled_buffer_25
  assign out_38 = Lodge ? {20{1'b0}} : 20'bz;  // Controlled_Buffer controlled_buffer_26
  assign out_29 = undriven ? in_12 : 20'bz;  // Controlled_Buffer controlled_buffer_27
  assign out_39 = Lodge ? {20{1'b0}} : 20'bz;  // Controlled_Buffer controlled_buffer_28
  assign out_30 = undriven ? in_11 : 20'bz;  // Controlled_Buffer controlled_buffer_29
  assign out_40 = Lodge ? {20{1'b0}} : 20'bz;  // Controlled_Buffer controlled_buffer_30
  not not_1 (Lodge, undriven);
  assign out_21 = Lodge ? adder_11_out : 20'bz;  // Controlled_Buffer controlled_buffer_31
  assign out_22 = Lodge ? adder_12_out : 20'bz;  // Controlled_Buffer controlled_buffer_32
  assign out_23 = Lodge ? adder_13_out : 20'bz;  // Controlled_Buffer controlled_buffer_33
  assign out_24 = Lodge ? adder_14_out : 20'bz;  // Controlled_Buffer controlled_buffer_34
  assign out_25 = Lodge ? adder_15_out : 20'bz;  // Controlled_Buffer controlled_buffer_35
  assign out_26 = Lodge ? adder_16_out : 20'bz;  // Controlled_Buffer controlled_buffer_36
  assign out_27 = Lodge ? adder_17_out : 20'bz;  // Controlled_Buffer controlled_buffer_37
  assign out_28 = Lodge ? adder_18_out : 20'bz;  // Controlled_Buffer controlled_buffer_38
  assign out_29 = Lodge ? adder_19_out : 20'bz;  // Controlled_Buffer controlled_buffer_39
  assign out_30 = Lodge ? adder_20_out : 20'bz;  // Controlled_Buffer controlled_buffer_40

  // Notes on the sheet:
  //   object
  //   background
  //   object
  //   bg
endmodule
