// Logisim project Tic-Tac-Toe.circ as structural Verilog: 1 circuit, main circuit main
module main (
);

  wire _1A, _1B, _1iA, _1iB, _2A, _2B, _2iA, _2iB, _3A, _3B, _3iA, _3iB, _4A, _4B, _4iA, _4iB, _5A, _5B,
       _5iA, _5iB, _6A, _6B, _6iA, _6iB, _7A, _7B, _7iA, _7iB, _8A, _8B, _8iA, _8iB, _9A, _9B, _9iA, _9iB, A,
       A_s_turn_out, and_1_out, and_2_out, and_3_out, and_4_out, and_5_out, and_6_out, and_7_out, and_8_out,
       and_9_out, and_10_out, and_11_out, and_12_out, and_13_out, and_14_out, and_15_out, and_16_out,
       and_17_out, and_18_out, and_19_out, and_20_out, and_21_out, and_22_out, and_23_out, and_24_out,
       and_25_out, and_26_out, and_27_out, and_28_out, and_29_out, and_30_out, and_31_out, and_32_out,
       and_33_out, and_34_out, and_35_out, B, B_s_turn_out, buffer_1_out, buffer_2_out, buffer_3_out,
       buffer_4_out, buffer_5_out, buffer_6_out, buffer_7_out, buffer_8_out, buffer_9_out, buffer_10_out,
       buffer_11_out, buffer_12_out, buffer_13_out, buffer_14_out, buffer_15_out, buffer_16_out,
       buffer_17_out, buffer_18_out, buffer_19_out, buffer_20_out, buffer_21_out, buffer_22_out,
       buffer_23_out, buffer_24_out, buffer_25_out, buffer_26_out, buffer_27_out, buffer_28_out,
       buffer_29_out, buffer_30_out, buffer_31_out, buffer_32_out, buffer_33_out, buffer_34_out,
       buffer_35_out, buffer_36_out, buffer_37_out, buffer_38_out, buffer_39_out, buffer_40_out,
       buffer_41_out, buffer_42_out, buffer_43_out, buffer_44_out, buffer_45_out, buffer_46_out,
       buffer_47_out, buffer_48_out, buffer_49_out, buffer_50_out, buffer_51_out, buffer_52_out,
       buffer_53_out, buffer_54_out, buffer_55_out, buffer_56_out, buffer_57_out, buffer_58_out,
       buffer_59_out, button_1_out, button_2_out, button_3_out, button_4_out, button_5_out, button_6_out,
       button_7_out, button_8_out, button_9_out, HR, not_1_out, not_2_out, not_3_out, not_4_out, not_5_out,
       not_6_out, not_7_out, not_8_out, not_9_out, not_10_out, not_11_out, not_12_out, not_13_out,
       not_14_out, not_15_out, not_16_out, not_17_out, not_18_out, OK, or_1_out, or_2_out, or_3_out,
       or_4_out, or_5_out, or_6_out, or_7_out, or_8_out, or_10_out, or_11_out, or_12_out, or_13_out,
       or_14_out, or_15_out, or_16_out, or_17_out, or_18_out, or_19_out, or_20_out, or_21_out, or_22_out,
       or_24_out, or_25_out, or_26_out, or_27_out, or_28_out, Player_A_Wins_out, Player_B_Wins_out, R,
       Reset_Counters_out, tR, ttR;
  wire [3:0] PA, PB;

  Button A_s_turn (.out(A_s_turn_out));
  Button B_s_turn (.out(B_s_turn_out));
  or or_1 (or_1_out, A_s_turn_out, HR);
  assign _2A = A ? buffer_2_out : 1'bz;  // Controlled_Buffer controlled_buffer_1
  assign _3A = A ? buffer_3_out : 1'bz;  // Controlled_Buffer controlled_buffer_2
  assign _1A = A ? buffer_1_out : 1'bz;  // Controlled_Buffer controlled_buffer_3
  assign _8A = A ? buffer_8_out : 1'bz;  // Controlled_Buffer controlled_buffer_4
  assign _6A = A ? buffer_6_out : 1'bz;  // Controlled_Buffer controlled_buffer_5
  assign _4A = A ? buffer_4_out : 1'bz;  // Controlled_Buffer controlled_buffer_6
  assign _7A = A ? buffer_7_out : 1'bz;  // Controlled_Buffer controlled_buffer_7
  assign _5A = A ? buffer_5_out : 1'bz;  // Controlled_Buffer controlled_buffer_8
  T_Flip_Flop t_ff_1 (
    .clk(and_1_out), .T(and_1_out), .Q(A), .Qn(B), .preset(or_1_out), .reset(B_s_turn_out));  // open: en
  or or_2 (or_2_out, buffer_9_out, buffer_8_out, buffer_7_out, buffer_6_out, buffer_5_out, buffer_4_out, buffer_3_out, buffer_2_out, buffer_1_out);
  and and_1 (and_1_out, OK, or_2_out);
  assign _5B = B ? buffer_5_out : 1'bz;  // Controlled_Buffer controlled_buffer_9
  assign _7B = B ? buffer_7_out : 1'bz;  // Controlled_Buffer controlled_buffer_10
  assign _8B = B ? buffer_8_out : 1'bz;  // Controlled_Buffer controlled_buffer_11
  assign _4B = B ? buffer_4_out : 1'bz;  // Controlled_Buffer controlled_buffer_12
  assign _6B = B ? buffer_6_out : 1'bz;  // Controlled_Buffer controlled_buffer_13
  assign _9B = B ? buffer_9_out : 1'bz;  // Controlled_Buffer controlled_buffer_14
  assign _9A = A ? buffer_9_out : 1'bz;  // Controlled_Buffer controlled_buffer_15
  T_Flip_Flop t_ff_2 (.clk(_1A), .T(_1A), .Q(_1iA), .reset(or_3_out));  // open: Qn, preset, en
  LED led_1 (.in(or_3_out));
  or or_3 (or_3_out, R, _1iB);
  T_Flip_Flop t_ff_3 (.clk(_4A), .T(_4A), .Q(_4iA), .reset(or_4_out));  // open: Qn, preset, en
  LED led_2 (.in(or_4_out));
  or or_4 (or_4_out, R, _4iB);
  T_Flip_Flop t_ff_4 (.clk(_7A), .T(_7A), .Q(_7iA), .reset(or_5_out));  // open: Qn, preset, en
  LED led_3 (.in(or_5_out));
  or or_5 (or_5_out, R, _7iB);
  buf buffer_1 (buffer_1_out, button_1_out);
  buf buffer_2 (buffer_2_out, button_3_out);
  buf buffer_3 (buffer_3_out, button_2_out);
  buf buffer_4 (buffer_4_out, button_6_out);
  buf buffer_5 (buffer_5_out, button_5_out);
  buf buffer_6 (buffer_6_out, button_4_out);
  buf buffer_7 (buffer_7_out, button_9_out);
  buf buffer_8 (buffer_8_out, button_8_out);
  buf buffer_9 (buffer_9_out, button_7_out);
  assign _2B = B ? buffer_2_out : 1'bz;  // Controlled_Buffer controlled_buffer_16
  assign _1B = B ? buffer_1_out : 1'bz;  // Controlled_Buffer controlled_buffer_17
  assign _3B = B ? buffer_3_out : 1'bz;  // Controlled_Buffer controlled_buffer_18
  T_Flip_Flop t_ff_5 (.clk(_2A), .T(_2A), .Q(_2iA), .reset(or_6_out));  // open: Qn, preset, en
  or or_6 (or_6_out, R, _2iB);
  LED led_4 (.in(or_6_out));
  T_Flip_Flop t_ff_6 (.clk(_5A), .T(_5A), .Q(_5iA), .reset(or_7_out));  // open: Qn, preset, en
  or or_7 (or_7_out, R, _5iB);
  LED led_5 (.in(or_7_out));
  T_Flip_Flop t_ff_7 (.clk(_8A), .T(_8A), .Q(_8iA), .reset(or_8_out));  // open: Qn, preset, en
  or or_8 (or_8_out, R, _8iB);
  LED led_6 (.in(or_8_out));
  LED led_7 (.in(HR));
  LED led_8 (.in(HR));
  Button RESET (.out(HR));
  or or_9 (R, HR, ttR, tR);
  Button button_1 (.out(button_1_out));
  Button button_2 (.out(button_2_out));
  Button button_3 (.out(button_3_out));
  Button button_4 (.out(button_4_out));
  Button button_5 (.out(button_5_out));
  Button button_6 (.out(button_6_out));
  Button button_7 (.out(button_7_out));
  Button button_8 (.out(button_8_out));
  Button button_9 (.out(button_9_out));
  Button TIE (.out(ttR));
  T_Flip_Flop t_ff_8 (.clk(_3A), .T(_3A), .Q(_3iA), .reset(or_10_out));  // open: Qn, preset, en
  LED led_9 (.in(or_10_out));
  or or_10 (or_10_out, R, _3iB);
  T_Flip_Flop t_ff_9 (.clk(_6A), .T(_6A), .Q(_6iA), .reset(or_11_out));  // open: Qn, preset, en
  LED led_10 (.in(or_11_out));
  or or_11 (or_11_out, R, _6iB);
  T_Flip_Flop t_ff_10 (.clk(_9A), .T(_9A), .Q(_9iA), .reset(or_12_out));  // open: Qn, preset, en
  or or_12 (or_12_out, R, _9iB);
  LED led_11 (.in(or_12_out));
  LED led_12 (.in(_1iA));
  LED led_13 (.in(_1iB));
  LED led_14 (.in(_1iB));
  LED led_15 (.in(_1iA));
  LED led_16 (.in(_1iA));
  LED led_17 (.in(_1iB));
  LED led_18 (.in(_1iB));
  LED led_19 (.in(_1iB));
  LED led_20 (.in(_1iA));
  LED led_21 (.in(_4iA));
  LED led_22 (.in(_4iB));
  LED led_23 (.in(_4iB));
  LED led_24 (.in(_4iA));
  LED led_25 (.in(_4iB));
  LED led_26 (.in(_4iA));
  LED led_27 (.in(_4iB));
  LED led_28 (.in(_4iB));
  LED led_29 (.in(_4iA));
  LED led_30 (.in(_7iB));
  LED led_31 (.in(_7iA));
  LED led_32 (.in(_7iB));
  LED led_33 (.in(_7iA));
  LED led_34 (.in(_7iB));
  LED led_35 (.in(_7iA));
  LED led_36 (.in(_7iA));
  LED led_37 (.in(_7iB));
  LED led_38 (.in(_7iB));
  T_Flip_Flop t_ff_11 (.clk(_1B), .T(_1B), .Q(_1iB), .reset(or_13_out));  // open: Qn, preset, en
  LED led_39 (.in(or_13_out));
  or or_13 (or_13_out, R, _1iA);
  T_Flip_Flop t_ff_12 (.clk(_4B), .T(_4B), .Q(_4iB), .reset(or_14_out));  // open: Qn, preset, en
  or or_14 (or_14_out, R, _4iA);
  LED led_40 (.in(or_14_out));
  T_Flip_Flop t_ff_13 (.clk(_7B), .T(_7B), .Q(_7iB), .reset(or_15_out));  // open: Qn, preset, en
  LED led_41 (.in(or_15_out));
  or or_15 (or_15_out, R, _7iA);
  LED Player_A (.in(A));
  LED Player_B (.in(B));
  LED led_42 (.in(_2iB));
  LED led_43 (.in(_2iA));
  LED led_44 (.in(_2iB));
  LED led_45 (.in(_5iB));
  LED led_46 (.in(_5iA));
  LED led_47 (.in(_5iB));
  LED led_48 (.in(_8iB));
  LED led_49 (.in(_8iA));
  LED led_50 (.in(_8iB));
  T_Flip_Flop t_ff_14 (.clk(_2B), .T(_2B), .Q(_2iB), .reset(or_16_out));  // open: Qn, preset, en
  or or_16 (or_16_out, R, _2iA);
  LED led_51 (.in(or_16_out));
  T_Flip_Flop t_ff_15 (.clk(_5B), .T(_5B), .Q(_5iB), .reset(or_17_out));  // open: Qn, preset, en
  LED led_52 (.in(or_17_out));
  or or_17 (or_17_out, R, _5iA);
  T_Flip_Flop t_ff_16 (.clk(_8B), .T(_8B), .Q(_8iB), .reset(or_18_out));  // open: Qn, preset, en
  or or_18 (or_18_out, R, _8iA);
  LED led_53 (.in(or_18_out));
  LED led_54 (.in(_2iB));
  LED led_55 (.in(_2iA));
  LED led_56 (.in(_2iB));
  LED led_57 (.in(_2iA));
  LED led_58 (.in(_2iA));
  LED led_59 (.in(_2iB));
  LED led_60 (.in(_5iA));
  LED led_61 (.in(_5iB));
  LED led_62 (.in(_5iA));
  LED led_63 (.in(_5iB));
  LED led_64 (.in(_5iA));
  LED led_65 (.in(_5iB));
  LED led_66 (.in(_8iB));
  LED led_67 (.in(_8iA));
  LED led_68 (.in(_8iA));
  LED led_69 (.in(_8iB));
  LED led_70 (.in(_8iB));
  LED led_71 (.in(_8iA));
  T_Flip_Flop t_ff_17 (.clk(_3B), .T(_3B), .Q(_3iB), .reset(or_19_out));  // open: Qn, preset, en
  or or_19 (or_19_out, R, _3iA);
  LED led_72 (.in(or_19_out));
  T_Flip_Flop t_ff_18 (.clk(_6B), .T(_6B), .Q(_6iB), .reset(or_20_out));  // open: Qn, preset, en
  LED led_73 (.in(or_20_out));
  or or_20 (or_20_out, R, _6iA);
  T_Flip_Flop t_ff_19 (.clk(_9B), .T(_9B), .Q(_9iB), .reset(or_21_out));  // open: Qn, preset, en
  or or_21 (or_21_out, R, _9iA);
  LED led_74 (.in(or_21_out));
  Hex_Digit_Display hex_digit_display_1 (.value(PA));  // open: dp
  LED led_75 (.in(_3iA));
  LED led_76 (.in(_3iB));
  LED led_77 (.in(_3iB));
  LED led_78 (.in(_3iA));
  LED led_79 (.in(_3iA));
  LED led_80 (.in(_3iB));
  LED led_81 (.in(_6iA));
  LED led_82 (.in(_6iB));
  LED led_83 (.in(_6iB));
  LED led_84 (.in(_6iA));
  LED led_85 (.in(_6iB));
  LED led_86 (.in(_6iA));
  LED led_87 (.in(_9iA));
  LED led_88 (.in(_9iB));
  LED led_89 (.in(_9iB));
  LED led_90 (.in(_9iA));
  LED led_91 (.in(_9iA));
  LED led_92 (.in(_9iB));
  Button Player_A_Wins (.out(Player_A_Wins_out));
  or or_22 (or_22_out, or_25_out, Player_A_Wins_out);
  Hex_Digit_Display hex_digit_display_2 (.value(PB));  // open: dp
  LED led_93 (.in(_3iB));
  LED led_94 (.in(_3iA));
  LED led_95 (.in(_3iB));
  LED led_96 (.in(_6iB));
  LED led_97 (.in(_6iA));
  LED led_98 (.in(_6iB));
  LED led_99 (.in(_9iB));
  LED led_100 (.in(_9iA));
  LED led_101 (.in(_9iB));
  or or_23 (tR, buffer_10_out, buffer_11_out);
  Button Reset_Counters (.out(Reset_Counters_out));
  buf buffer_10 (buffer_10_out, or_22_out);
  buf buffer_11 (buffer_11_out, or_24_out);
  Counter #(.width(4), .max('h8)) counter_1 (
    .count(or_22_out), .Q(PA), .clk(or_22_out), .clr(Reset_Counters_out));  // open: load, D, carry
  buf buffer_12 (buffer_12_out, _1iA);
  and and_2 (and_2_out, buffer_12_out, buffer_13_out, buffer_14_out);
  buf buffer_13 (buffer_13_out, _2iA);
  buf buffer_14 (buffer_14_out, _3iA);
  buf buffer_15 (buffer_15_out, _4iA);
  buf buffer_16 (buffer_16_out, _5iA);
  and and_3 (and_3_out, buffer_15_out, buffer_16_out, buffer_17_out);
  buf buffer_17 (buffer_17_out, _6iA);
  buf buffer_18 (buffer_18_out, _7iA);
  buf buffer_19 (buffer_19_out, _8iA);
  and and_4 (and_4_out, buffer_18_out, buffer_19_out, buffer_20_out);
  buf buffer_20 (buffer_20_out, _9iA);
  and and_5 (and_5_out, _1A, not_1_out);
  not not_1 (not_1_out, _1iB);
  and and_6 (and_6_out, _2A, not_2_out);
  not not_2 (not_2_out, _2iB);
  and and_7 (and_7_out, _3A, not_3_out);
  not not_3 (not_3_out, _3iB);
  and and_8 (and_8_out, _1B, not_4_out);
  not not_4 (not_4_out, _1iA);
  and and_9 (and_9_out, _2B, not_5_out);
  not not_5 (not_5_out, _2iA);
  and and_10 (and_10_out, _3B, not_6_out);
  not not_6 (not_6_out, _3iA);
  Button Player_B_Wins (.out(Player_B_Wins_out));
  or or_24 (or_24_out, Player_B_Wins_out, or_26_out);
  Counter #(.width(4), .max('h8)) counter_2 (
    .count(or_24_out), .Q(PB), .clk(or_24_out), .clr(Reset_Counters_out));  // open: load, D, carry
  buf buffer_21 (buffer_21_out, _1iA);
  and and_11 (and_11_out, buffer_21_out, buffer_22_out, buffer_23_out);
  buf buffer_22 (buffer_22_out, _4iA);
  buf buffer_23 (buffer_23_out, _7iA);
  buf buffer_24 (buffer_24_out, _2iA);
  buf buffer_25 (buffer_25_out, _5iA);
  and and_12 (and_12_out, buffer_24_out, buffer_25_out, buffer_26_out);
  buf buffer_26 (buffer_26_out, _8iA);
  buf buffer_27 (buffer_27_out, _3iA);
  and and_13 (and_13_out, buffer_27_out, buffer_28_out, buffer_29_out);
  buf buffer_28 (buffer_28_out, _6iA);
  buf buffer_29 (buffer_29_out, _9iA);
  or or_25 (or_25_out, and_4_out, and_3_out, and_2_out, and_13_out, and_12_out, and_11_out, and_15_out, and_14_out);
  not not_7 (not_7_out, _4iB);
  not not_8 (not_8_out, _5iB);
  not not_9 (not_9_out, _6iB);
  not not_10 (not_10_out, _4iA);
  not not_11 (not_11_out, _5iA);
  not not_12 (not_12_out, _6iA);
  buf buffer_30 (buffer_30_out, _1iA);
  and and_14 (and_14_out, buffer_30_out, buffer_31_out, buffer_32_out);
  buf buffer_31 (buffer_31_out, _5iA);
  buf buffer_32 (buffer_32_out, _9iA);
  buf buffer_33 (buffer_33_out, _3iA);
  and and_15 (and_15_out, buffer_33_out, buffer_34_out, buffer_35_out);
  buf buffer_34 (buffer_34_out, _5iA);
  buf buffer_35 (buffer_35_out, _7iA);
  and and_16 (and_16_out, _4A, not_7_out);
  and and_17 (and_17_out, _5A, not_8_out);
  and and_18 (and_18_out, _6A, not_9_out);
  and and_19 (and_19_out, _4B, not_10_out);
  and and_20 (and_20_out, _5B, not_11_out);
  and and_21 (and_21_out, _6B, not_12_out);
  buf buffer_36 (buffer_36_out, _1iB);
  buf buffer_37 (buffer_37_out, _2iB);
  buf buffer_38 (buffer_38_out, _3iB);
  buf buffer_39 (buffer_39_out, _4iB);
  buf buffer_40 (buffer_40_out, _5iB);
  buf buffer_41 (buffer_41_out, _6iB);
  buf buffer_42 (buffer_42_out, _7iB);
  buf buffer_43 (buffer_43_out, _8iB);
  buf buffer_44 (buffer_44_out, _9iB);
  and and_22 (and_22_out, _7A, not_13_out);
  not not_13 (not_13_out, _7iB);
  and and_23 (and_23_out, _8A, not_14_out);
  not not_14 (not_14_out, _8iB);
  and and_24 (and_24_out, _9A, not_15_out);
  not not_15 (not_15_out, _9iB);
  and and_25 (and_25_out, _7B, not_16_out);
  not not_16 (not_16_out, _7iA);
  and and_26 (and_26_out, _8B, not_17_out);
  not not_17 (not_17_out, _8iA);
  and and_27 (and_27_out, _9B, not_18_out);
  not not_18 (not_18_out, _9iA);
  buf buffer_45 (buffer_45_out, _1iB);
  buf buffer_46 (buffer_46_out, _4iB);
  and and_28 (and_28_out, buffer_36_out, buffer_37_out, buffer_38_out);
  buf buffer_47 (buffer_47_out, _7iB);
  buf buffer_48 (buffer_48_out, _2iB);
  buf buffer_49 (buffer_49_out, _5iB);
  and and_29 (and_29_out, buffer_39_out, buffer_40_out, buffer_41_out);
  buf buffer_50 (buffer_50_out, _8iB);
  buf buffer_51 (buffer_51_out, _3iB);
  and and_30 (and_30_out, buffer_42_out, buffer_43_out, buffer_44_out);
  buf buffer_52 (buffer_52_out, _6iB);
  buf buffer_53 (buffer_53_out, _9iB);
  or or_26 (or_26_out, and_30_out, and_29_out, and_28_out, and_33_out, and_32_out, and_31_out, and_35_out, and_34_out);
  and and_31 (and_31_out, buffer_45_out, buffer_46_out, buffer_47_out);
  and and_32 (and_32_out, buffer_48_out, buffer_49_out, buffer_50_out);
  and and_33 (and_33_out, buffer_51_out, buffer_52_out, buffer_53_out);
  assign OK = A ? or_27_out : 1'bz;  // Controlled_Buffer controlled_buffer_19
  or or_27 (or_27_out, and_5_out, and_16_out, and_22_out, and_17_out, and_23_out, and_18_out, and_7_out, and_24_out, and_6_out);
  assign OK = B ? or_28_out : 1'bz;  // Controlled_Buffer controlled_buffer_20
  or or_28 (or_28_out, and_8_out, and_19_out, and_25_out, and_20_out, and_26_out, and_21_out, and_10_out, and_27_out, and_9_out);
  buf buffer_54 (buffer_54_out, _1iB);
  buf buffer_55 (buffer_55_out, _5iB);
  and and_34 (and_34_out, buffer_54_out, buffer_55_out, buffer_56_out);
  buf buffer_56 (buffer_56_out, _9iB);
  buf buffer_57 (buffer_57_out, _3iB);
  and and_35 (and_35_out, buffer_57_out, buffer_58_out, buffer_59_out);
  buf buffer_58 (buffer_58_out, _5iB);
  buf buffer_59 (buffer_59_out, _7iB);

  // Other names for the same wires on the sheet: R1AB = _1iA; R1BA = _1iB; R2AB = _2iA; R2BA = _2iB; R3AB = _3iA;
  //   R3BA = _3iB; R4AB = _4iA; R4BA = _4iB; R5AB = _5iA; R5BA = _5iB; R6AB = _6iA; R6BA = _6iB; R7AB = _7iA;
  //   R7BA = _7iB; R8AB = _8iA; R8BA = _8iB; R9AB = _9iA; R9BA = _9iB
endmodule
