// Logisim project Watch.circ as structural Verilog: 1 circuit, main circuit main
module main (
);

  wire and_1_out, and_2_out, and_3_out, and_4_out, button_1_out, clock_1_out, comparator_1_eq,
       comparator_2_eq, comparator_3_eq, comparator_4_eq, comparator_5_eq, comparator_6_eq, comparator_7_eq,
       not_1_out, or_1_out, or_2_out, or_3_out, or_4_out, or_5_out, or_6_out, or_7_out, or_8_out, or_9_out,
       or_10_out, or_11_out, or_12_out, shift_register_1_out, shift_register_1_q0, shift_register_1_q1,
       shift_register_1_q2, shift_register_1_q3, shift_register_1_q4, shift_register_1_q5,
       shift_register_1_q6, shift_register_1_q7, shift_register_1_q8, shift_register_1_q9,
       shift_register_1_q10, shift_register_1_q11, shift_register_1_q12, shift_register_1_q13,
       shift_register_1_q14, shift_register_1_q15, shift_register_1_q16, shift_register_1_q17,
       shift_register_1_q18, shift_register_1_q19, shift_register_1_q20, shift_register_1_q21,
       shift_register_1_q22, shift_register_1_q23, shift_register_1_q24, shift_register_1_q25,
       shift_register_1_q26, shift_register_1_q27, shift_register_1_q28, shift_register_1_q29,
       shift_register_2_out, shift_register_2_q0, shift_register_2_q1, shift_register_2_q2,
       shift_register_2_q3, shift_register_2_q4, shift_register_2_q5, shift_register_2_q6,
       shift_register_2_q7, shift_register_2_q8, shift_register_2_q9, shift_register_2_q10,
       shift_register_2_q11, shift_register_2_q12, shift_register_2_q13, shift_register_2_q14,
       shift_register_2_q15, shift_register_2_q16, shift_register_2_q17, shift_register_2_q18,
       shift_register_2_q19, shift_register_2_q20, shift_register_2_q21, shift_register_2_q22,
       shift_register_2_q23, shift_register_2_q24, shift_register_2_q25, shift_register_2_q26,
       shift_register_2_q27, shift_register_2_q28, shift_register_2_q29, t_ff_1_q, t_ff_1_qn, t_ff_2_q;
  wire [3:0] counter_1_q, counter_2_q, counter_3_q, counter_4_q, counter_5_q, counter_6_q;

  Clock clock_1 (.out(clock_1_out));
  Button button_1 (.out(button_1_out));
  Hex_Digit_Display hex_digit_display_1 (.value(counter_1_q));  // open: dp
  Hex_Digit_Display hex_digit_display_2 (.value(counter_2_q));  // open: dp
  Counter #(.width(4), .max('h9)) counter_1 (
    .count(shift_register_2_out), .Q(counter_1_q), .clk(shift_register_2_out), .clr(or_1_out));  // open: load, D, carry
  or or_1 (or_1_out, and_3_out, or_7_out);
  Counter #(.width(4), .max('h1)) counter_2 (
    .count(comparator_5_eq), .Q(counter_2_q), .clk(comparator_5_eq), .clr(or_2_out));  // open: load, D, carry
  or or_2 (or_2_out, and_3_out, or_7_out);
  LED led_1 (.in(clock_1_out));
  LED led_2 (.in(clock_1_out));
  Hex_Digit_Display hex_digit_display_3 (.value(counter_3_q));  // open: dp
  Counter #(.width(4), .max('h5)) counter_3 (
    .count(comparator_7_eq), .Q(counter_3_q), .clk(comparator_7_eq), .clr(or_3_out));  // open: load, D, carry
  or or_3 (or_3_out, shift_register_2_out, or_7_out);
  LED led_3 (.in(clock_1_out));
  LED led_4 (.in(clock_1_out));
  Hex_Digit_Display hex_digit_display_4 (.value(counter_4_q));  // open: dp
  Counter #(.width(4), .max('h9)) counter_4 (
    .count(and_1_out), .Q(counter_4_q), .clk(and_1_out), .clr(or_4_out));  // open: load, D, carry
  or or_4 (or_4_out, shift_register_2_out, or_7_out);
  Hex_Digit_Display hex_digit_display_5 (.value(counter_6_q));  // open: dp
  Hex_Digit_Display hex_digit_display_6 (.value(counter_5_q));  // open: dp
  Counter #(.width(4), .max('h9)) counter_5 (
    .count(clock_1_out), .Q(counter_5_q), .clk(clock_1_out), .clr(or_5_out));  // open: load, D, carry
  or or_5 (or_5_out, and_1_out, or_7_out);
  Counter #(.width(4), .max('h6)) counter_6 (
    .count(comparator_1_eq), .Q(counter_6_q), .clk(comparator_1_eq), .clr(or_6_out));  // open: load, D, carry
  or or_6 (or_6_out, and_1_out, or_7_out);
  or or_7 (or_7_out, and_3_out, button_1_out);
  LED PM (.in(t_ff_1_q));
  LED AM (.in(t_ff_1_qn));
  Comparator #(.width(4)) comparator_1 (.a(counter_5_q), .b(4'b0000), .eq(comparator_1_eq));  // open: gt, lt
  Comparator #(.width(4)) comparator_2 (.a(counter_6_q), .b(4'b0110), .eq(comparator_2_eq));  // open: gt, lt
  Comparator #(.width(4)) comparator_3 (.a(counter_4_q), .b(4'b1001), .eq(comparator_3_eq));  // open: gt, lt
  Comparator #(.width(4)) comparator_4 (.a(counter_3_q), .b(4'b0101), .eq(comparator_4_eq));  // open: gt, lt
  Comparator #(.width(4)) comparator_5 (.a(counter_1_q), .b(4'b0011), .eq(comparator_5_eq));  // open: gt, lt
  Comparator #(.width(4)) comparator_6 (.a(counter_2_q), .b(4'b0001), .eq(comparator_6_eq));  // open: gt, lt
  and and_1 (and_1_out, comparator_1_eq, comparator_2_eq);
  and and_2 (and_2_out, comparator_3_eq, comparator_4_eq);
  and and_3 (and_3_out, comparator_5_eq, comparator_6_eq);
  Comparator #(.width(4)) comparator_7 (.a(counter_4_q), .b(4'b0000), .eq(comparator_7_eq));  // open: gt, lt
  T_Flip_Flop t_ff_1 (.clk(or_7_out), .T(or_7_out), .Q(t_ff_1_q), .Qn(t_ff_1_qn));  // open: preset, reset, en
  T_Flip_Flop t_ff_2 (.clk(and_2_out), .T(and_2_out), .Q(t_ff_2_q), .reset(not_1_out));  // open: Qn, preset, en
  and and_4 (and_4_out, t_ff_2_q, ~or_10_out);  // AND_Gate
  not not_1 (not_1_out, clock_1_out);
  Shift_Register #(.length(30)) shift_register_1 (
    .in(and_4_out), .clk(not_1_out), .out(shift_register_1_out), .q0(shift_register_1_q0),
    .q1(shift_register_1_q1), .q2(shift_register_1_q2), .q3(shift_register_1_q3), .q4(shift_register_1_q4),
    .q5(shift_register_1_q5), .q6(shift_register_1_q6), .q7(shift_register_1_q7), .q8(shift_register_1_q8),
    .q9(shift_register_1_q9), .q10(shift_register_1_q10), .q11(shift_register_1_q11),
    .q12(shift_register_1_q12), .q13(shift_register_1_q13), .q14(shift_register_1_q14),
    .q15(shift_register_1_q15), .q16(shift_register_1_q16), .q17(shift_register_1_q17),
    .q18(shift_register_1_q18), .q19(shift_register_1_q19), .q20(shift_register_1_q20),
    .q21(shift_register_1_q21), .q22(shift_register_1_q22), .q23(shift_register_1_q23),
    .q24(shift_register_1_q24), .q25(shift_register_1_q25), .q26(shift_register_1_q26),
    .q27(shift_register_1_q27), .q28(shift_register_1_q28), .q29(shift_register_1_q29));  // open: shift, load, clr, d0, d1, d2, d3, d4, d5, d6, d7, d8, d9, d10, d11, d12, d13, d14, d15, d16, d17, d18, d19, d20, d21, d22, d23, d24, d25, d26, d27, d28, d29
  or or_8 (or_8_out, shift_register_1_q0, shift_register_1_q1, shift_register_1_q2, shift_register_1_q3, shift_register_1_q4, shift_register_1_q5, shift_register_1_q6, shift_register_1_q7, shift_register_1_q8, shift_register_1_q9, shift_register_1_q10, shift_register_1_q11, shift_register_1_q12, shift_register_1_q13, shift_register_1_q14);
  or or_9 (or_9_out, shift_register_1_q15, shift_register_1_q16, shift_register_1_q17, shift_register_1_q18, shift_register_1_q19, shift_register_1_q20, shift_register_1_q21, shift_register_1_q22, shift_register_1_q23, shift_register_1_q24, shift_register_1_q25, shift_register_1_q26, shift_register_1_q27, shift_register_1_q28, shift_register_1_q29);
  Shift_Register #(.length(30)) shift_register_2 (
    .in(shift_register_1_out), .clk(not_1_out), .out(shift_register_2_out), .q0(shift_register_2_q0),
    .q1(shift_register_2_q1), .q2(shift_register_2_q2), .q3(shift_register_2_q3), .q4(shift_register_2_q4),
    .q5(shift_register_2_q5), .q6(shift_register_2_q6), .q7(shift_register_2_q7), .q8(shift_register_2_q8),
    .q9(shift_register_2_q9), .q10(shift_register_2_q10), .q11(shift_register_2_q11),
    .q12(shift_register_2_q12), .q13(shift_register_2_q13), .q14(shift_register_2_q14),
    .q15(shift_register_2_q15), .q16(shift_register_2_q16), .q17(shift_register_2_q17),
    .q18(shift_register_2_q18), .q19(shift_register_2_q19), .q20(shift_register_2_q20),
    .q21(shift_register_2_q21), .q22(shift_register_2_q22), .q23(shift_register_2_q23),
    .q24(shift_register_2_q24), .q25(shift_register_2_q25), .q26(shift_register_2_q26),
    .q27(shift_register_2_q27), .q28(shift_register_2_q28), .q29(shift_register_2_q29));  // open: shift, load, clr, d0, d1, d2, d3, d4, d5, d6, d7, d8, d9, d10, d11, d12, d13, d14, d15, d16, d17, d18, d19, d20, d21, d22, d23, d24, d25, d26, d27, d28, d29
  or or_10 (or_10_out, or_8_out, or_9_out, or_11_out, or_12_out);
  or or_11 (or_11_out, shift_register_2_q0, shift_register_2_q1, shift_register_2_q2, shift_register_2_q3, shift_register_2_q4, shift_register_2_q5, shift_register_2_q6, shift_register_2_q7, shift_register_2_q8, shift_register_2_q9, shift_register_2_q10, shift_register_2_q11, shift_register_2_q12, shift_register_2_q13, shift_register_2_q14);
  or or_12 (or_12_out, shift_register_2_q15, shift_register_2_q16, shift_register_2_q17, shift_register_2_q18, shift_register_2_q19, shift_register_2_q20, shift_register_2_q21, shift_register_2_q22, shift_register_2_q23, shift_register_2_q24, shift_register_2_q25, shift_register_2_q26, shift_register_2_q27, shift_register_2_q28, shift_register_2_q29);
endmodule
